# Fritzing sketch Sensors.2 (saved by Fritzing 1.0.3b)

parts:
  HC-SR04_Sensor_1 = HC-SR04 Ultrasonic Distance Sensor
  MIC1 = Microphone
  Raspberry_Pi_1 = Raspberry Pi 3 [part_number=RPI-3-V1.2]
  TTP223B1 = TTP223B Capacitive Touch Sensor Module
  M1 = Humidity and Temperature Sensor DHT11
  Part2 = HC-SR501 Body Sensor Module
  Grove1 = Grove Light Sensor
  SP1 = SPEAKER [package=pcb_mount_speaker]  # not connected
  Part3 = Flat Ribbon  # not connected
  Conn_8 = USB connector [package=THT]

nets:
  N1: HC-SR04_Sensor_1.TRIG, Raspberry_Pi_1.GPIO4
  N2: HC-SR04_Sensor_1.ECHO, Raspberry_Pi_1.GPIO17
  N3: MIC1.pin1, Conn_8.5V
  N4: Raspberry_Pi_1.GPIO6, Part2.OUT
  N5: Raspberry_Pi_1.GPIO19, Grove1.SIG
  N6: Raspberry_Pi_1.GPIO26, M1.GND
  N7: Raspberry_Pi_1.GPIO21, TTP223B1.SIG

custom parts:
  TTP223B Capacitive Touch Sensor Module: The TTP223B capacitive touch sensor module uses the TTP223B IC. The appropriate voltage is approximately 2 to 5.5 volts.
  Humidity and Temperature Sensor DHT11: Digital relative humidity & temperature sensor DHT11
  HC-SR501 Body Sensor Module: Pyroelectric Infrared PIR Motion Sensor Detector Module
  Grove Light Sensor: An analog light sensor
